# Fritzing sketch class_button (saved by Fritzing 0.7.12b)
breadboards: 1

parts:
  Arduino1 = Arduino
  S1 = Pushbutton [package="[THT]"]

nets:
  N1: Arduino1.GND, S1.Pin_1, S1.Pin_2
  N2: Arduino1.D2, S1.Pin_3, S1.Pin_4
